// Logisim project assignment2.circ as structural Verilog
module Q1_AND_OR (
  input  a,
  input  b,
  input  c,
  input  d,
  output out1,
  output out2
);

  and and_1 (out1, a, b, c, d);
  or or_1 (out2, a, b, c, d);

  // Notes on the sheet:
  //   Q1 | Four-input AND and OR
endmodule

module Q2_MUX8 (
  input  [7:0] d,
  input  [2:0] s,
  output y
);

  Multiplexer #(.select(3), .enable("false")) multiplexer_1 (
    .in0(d[0]), .in1(d[1]), .in2(d[2]), .in3(d[3]), .in4(d[4]), .in5(d[5]), .in6(d[6]), .in7(d[7]), .out(y),
    .sel(s));

  // Notes on the sheet:
  //   Q2 | s=000 selects d[0]; s=111 selects d[7]
endmodule

module Q3_LETTERS (
  input  [2:0] sel,
  output [7:0] seg
);

  ROM #(.addrWidth(3), .dataWidth(8)) Letter_lookup (.addr(sel), .data(seg));
  _7_Segment_Display u_7_segment_display_1 (
    .g(seg[1]), .f(seg[2]), .a(seg[7]), .b(seg[6]), .e(seg[3]), .d(seg[4]), .c(seg[5]), .dp(seg[0]));

  // Other names for the same wires on the sheet: dp = seg[0]; g = seg[1]; f = seg[2]; e = seg[3]; d = seg[4];
  //   c = seg[5]; b = seg[6]; a = seg[7]

  // Notes on the sheet:
  //   Q3 | sel=0..5: A,b,C,d,F,G; sel=6,7: blank
  //   contents of Letter_lookup (hex, n*v repeats v):
  //   ee 3e 9c 7a 8e be 0 0
  //   Active high: seg[7:0] = a b c d e f g dp
endmodule

module Q4_VOTING25 (
  input  [24:0] vt,
  output result,
  output [4:0] count
);

  BitAdder #(.width(25)) bitadder_1 (.in0(vt), .out(count));
  Comparator #(.width(5), .mode("unsigned")) comparator_1 (.a(count), .b(5'b01100), .gt(result));  // open: eq, lt

  // Notes on the sheet:
  //   Q4 | 25 voters: result=1 if at least 13 votes are 1
endmodule

module Q5_COUNT_DISPLAY (
  input  [12:0] vt,
  input  en,
  output [7:0] seg
);

  wire [3:0] count;
  wire [7:0] decoded;

  BitAdder #(.width(13)) bitadder_1 (.in0(vt), .out(count));
  ROM #(.addrWidth(4), .dataWidth(8)) Hex_lookup (.addr(count), .data(decoded));
  Multiplexer #(.select(1), .width(8), .enable("false")) multiplexer_1 (
    .in0({8{1'b0}}), .in1(decoded), .out(seg), .sel(en));
  _7_Segment_Display u_7_segment_display_1 (
    .g(seg[1]), .f(seg[2]), .a(seg[7]), .b(seg[6]), .e(seg[3]), .d(seg[4]), .c(seg[5]), .dp(seg[0]));

  // Other names for the same wires on the sheet: dp = seg[0]; g = seg[1]; f = seg[2]; e = seg[3]; d = seg[4];
  //   c = seg[5]; b = seg[6]; a = seg[7]

  // Notes on the sheet:
  //   Q5 | Count vt[12:0]; en=0 blanks the display
  //   Counts 0..13 are reachable; E,F are decoder-only test cases.
  //   contents of Hex_lookup (hex, n*v repeats v):
  //   fc 60 da f2 66 b6 be e0 fe f6 ee 3e 9c 7a 9e 8e
  //   Active high: seg[7:0] = a b c d e f g dp
endmodule

module VHDL_and_or4 (
  input  a,
  input  b,
  input  c,
  input  d,
  output out1,
  output out2
);

  and_or4 U1 (.a(a), .b(b), .c(c), .d(d), .out1(out1), .out2(out2));

  // Notes on the sheet:
  //   VHDL | and_or4 (enable VHDL Simulation / Questa)
endmodule

module VHDL_mux8 (
  input  [7:0] d,
  input  [2:0] s,
  output y
);

  mux8 U1 (.d(d), .s(s), .y(y));

  // Notes on the sheet:
  //   VHDL | mux8 (enable VHDL Simulation / Questa)
endmodule

module VHDL_letters7seg (
  input  [2:0] sel,
  output [7:0] seg
);

  letters7seg U1 (.sel(sel), .seg(seg));
  _7_Segment_Display u_7_segment_display_1 (
    .g(seg[1]), .f(seg[2]), .a(seg[7]), .b(seg[6]), .e(seg[3]), .d(seg[4]), .c(seg[5]), .dp(seg[0]));

  // Other names for the same wires on the sheet: dp = seg[0]; g = seg[1]; f = seg[2]; e = seg[3]; d = seg[4];
  //   c = seg[5]; b = seg[6]; a = seg[7]

  // Notes on the sheet:
  //   VHDL | letters7seg (enable VHDL Simulation / Questa)
  //   Active high: seg[7:0] = a b c d e f g dp
endmodule

module VHDL_voting25 (
  input  [24:0] vt,
  output result
);

  voting25 U1 (.vt(vt), .result(result));

  // Notes on the sheet:
  //   VHDL | voting25 (enable VHDL Simulation / Questa)
endmodule

module VHDL_popcount13_display (
  input  [12:0] vt,
  input  en,
  output [7:0] seg
);

  popcount13_display U1 (.vt(vt), .en(en), .seg(seg));
  _7_Segment_Display u_7_segment_display_1 (
    .g(seg[1]), .f(seg[2]), .a(seg[7]), .b(seg[6]), .e(seg[3]), .d(seg[4]), .c(seg[5]), .dp(seg[0]));

  // Other names for the same wires on the sheet: dp = seg[0]; g = seg[1]; f = seg[2]; e = seg[3]; d = seg[4];
  //   c = seg[5]; b = seg[6]; a = seg[7]

  // Notes on the sheet:
  //   VHDL | popcount13_display (enable VHDL Simulation / Questa)
  //   Active high: seg[7:0] = a b c d e f g dp
endmodule

// VHDL entity and_or4, as the project stores it:
library ieee;
use ieee.std_logic_1164.all;
use ieee.numeric_std.all;

entity and_or4 is
  port (a, b, c, d : in std_logic;
        out1, out2 : out std_logic);
end and_or4;

architecture rtl of and_or4 is
begin
  out1 <= a and b and c and d;
  out2 <= a or b or c or d;
end rtl;

// VHDL entity mux8, as the project stores it:
library ieee;
use ieee.std_logic_1164.all;
use ieee.numeric_std.all;

entity mux8 is
  port (d : in std_logic_vector(7 downto 0);
        s : in std_logic_vector(2 downto 0);
        y : out std_logic);
end mux8;

architecture rtl of mux8 is
begin
  -- s=000 selects d(0), s=111 selects d(7).
  with s select y <=
    d(0) when "000", d(1) when "001",
    d(2) when "010", d(3) when "011",
    d(4) when "100", d(5) when "101",
    d(6) when "110", d(7) when "111",
    'X' when others;
end rtl;

// VHDL entity letters7seg, as the project stores it:
library ieee;
use ieee.std_logic_1164.all;
use ieee.numeric_std.all;

entity letters7seg is
  port (sel : in std_logic_vector(2 downto 0);
        seg : out std_logic_vector(7 downto 0));
end letters7seg;

architecture rtl of letters7seg is
begin
  -- seg(7 downto 0) = a,b,c,d,e,f,g,dp; 1 turns a segment on.
  -- 000..101: a,b,c,d,f,g (A,b,C,d,F,G on seven segments).
  with sel select seg <=
    "11101110" when "000",
    "00111110" when "001",
    "10011100" when "010",
    "01111010" when "011",
    "10001110" when "100",
    "10111110" when "101",
    "00000000" when others;
end rtl;

// VHDL entity voting25, as the project stores it:
library ieee;
use ieee.std_logic_1164.all;
use ieee.numeric_std.all;

entity voting25 is
  port (vt : in std_logic_vector(24 downto 0);
        result : out std_logic);
end voting25;

architecture rtl of voting25 is
begin
  process(vt)
    variable count : integer range 0 to 25;
    variable valid : boolean;
  begin
    count := 0;
    valid := true;
    for i in vt'range loop
      if vt(i) = '1' then count := count + 1;
      elsif vt(i) /= '0' then valid := false;
      end if;
    end loop;
    if not valid then result <= 'X';
    elsif count >= 13 then result <= '1';
    else result <= '0';
    end if;
  end process;
end rtl;

// VHDL entity popcount13_display, as the project stores it:
library ieee;
use ieee.std_logic_1164.all;
use ieee.numeric_std.all;

entity popcount13_display is
  port (vt : in std_logic_vector(12 downto 0);
        en : in std_logic;
        seg : out std_logic_vector(7 downto 0));
end popcount13_display;

architecture rtl of popcount13_display is
begin
  process(vt, en)
    variable count : integer range 0 to 13;
    variable valid : boolean;
  begin
    count := 0;
    valid := true;
    for i in vt'range loop
      if vt(i) = '1' then count := count + 1;
      elsif vt(i) /= '0' then valid := false;
      end if;
    end loop;
    if en = '0' then seg <= "00000000";
    elsif en /= '1' or not valid then seg <= (others => 'X');
    else
      case count is
        when 0 => seg <= "11111100";
        when 1 => seg <= "01100000";
        when 2 => seg <= "11011010";
        when 3 => seg <= "11110010";
        when 4 => seg <= "01100110";
        when 5 => seg <= "10110110";
        when 6 => seg <= "10111110";
        when 7 => seg <= "11100000";
        when 8 => seg <= "11111110";
        when 9 => seg <= "11110110";
        when 10 => seg <= "11101110";
        when 11 => seg <= "00111110";
        when 12 => seg <= "10011100";
        when 13 => seg <= "01111010";
        -- E and F are defined for a reusable hexadecimal decoder;
        -- 14 and 15 are unreachable with a 13-bit input.
        when others => seg <= "00000000";
      end case;
    end if;
  end process;
end rtl;

// VHDL entity hex7seg, as the project stores it:
library ieee;
use ieee.std_logic_1164.all;
use ieee.numeric_std.all;

entity hex7seg is
  port (n : in std_logic_vector(3 downto 0);
        seg : out std_logic_vector(7 downto 0));
end hex7seg;

architecture rtl of hex7seg is
begin
  -- seg = abcdefg dp, active high.
  with n select seg <=
    "11111100" when "0000",
    "01100000" when "0001",
    "11011010" when "0010",
    "11110010" when "0011",
    "01100110" when "0100",
    "10110110" when "0101",
    "10111110" when "0110",
    "11100000" when "0111",
    "11111110" when "1000",
    "11110110" when "1001",
    "11101110" when "1010",
    "00111110" when "1011",
    "10011100" when "1100",
    "01111010" when "1101",
    "10011110" when "1110",
    "10001110" when "1111",
    (others => 'X') when others;
end rtl;
