// Logisim project sequential_logic.circ as structural Verilog: 5 circuits, main circuit rs_latch
module rs_latch (
  input  s,
  input  r,
  output q,
  output qb
);

  nor G1 (q, r, qb);
  nor G2 (qb, s, q);

  // Notes on the sheet:
  //   rs_latch | Gate-level only | Same-name tunnels are connected
endmodule

module d_latch (
  input  d,
  input  en,
  output q,
  output qb
);

  wire dn, rb, sb;

  nand G1 (dn, d, d);
  nand G2 (sb, d, en);
  nand G3 (rb, dn, en);
  nand G4 (q, sb, qb);
  nand G5 (qb, rb, q);

  // Notes on the sheet:
  //   d_latch | Gate-level only | Same-name tunnels are connected
endmodule

module d_ff (
  input  d,
  input  clk,
  output q,
  output qb
);

  wire clkn, m_dn, m_rb, m_sb, mq, mqb, s_dn, s_rb, s_sb;

  not G1 (clkn, clk);
  nand G2 (m_dn, d, d);
  nand G3 (m_sb, d, clkn);
  nand G4 (m_rb, m_dn, clkn);
  nand G5 (mq, m_sb, mqb);
  nand G6 (mqb, m_rb, mq);
  nand G7 (s_dn, mq, mq);
  nand G8 (s_sb, mq, clk);
  nand G9 (s_rb, s_dn, clk);
  nand G10 (q, s_sb, qb);
  nand G11 (qb, s_rb, q);

  // Notes on the sheet:
  //   d_ff | Gate-level only | Same-name tunnels are connected
endmodule

module jk_ff (
  input  j,
  input  k,
  input  clk,
  input  clr_n,
  output q,
  output qb
);

  wire clkn, jterm, kn, kterm, m_clear_ab, m_clear_n, m_dn, m_rb, m_sb, men, men_n, mq, mqb, next_d,
       s_clear_ab, s_clear_n, s_dn, s_rb, s_sb, sen, sen_n;

  nand G1 (clkn, clk, clk);
  nand G2 (kn, k, k);
  nand G3 (jterm, j, qb);
  nand G4 (kterm, kn, q);
  nand G5 (next_d, jterm, kterm);
  nand G6 (men_n, clkn, clr_n);
  nand G7 (men, men_n, men_n);
  nand G8 (sen_n, clk, clr_n);
  nand G9 (sen, sen_n, sen_n);
  nand G10 (m_dn, next_d, next_d);
  nand G11 (m_sb, next_d, men);
  nand G12 (m_rb, m_dn, men);
  nand G13 (mq, m_sb, mqb);
  nand G14 (m_clear_n, m_rb, mq);
  nand G15 (m_clear_ab, m_clear_n, m_clear_n);
  nand G16 (mqb, m_clear_ab, clr_n);
  nand G17 (s_dn, mq, mq);
  nand G18 (s_sb, mq, sen);
  nand G19 (s_rb, s_dn, sen);
  nand G20 (q, s_sb, qb);
  nand G21 (s_clear_n, s_rb, q);
  nand G22 (s_clear_ab, s_clear_n, s_clear_n);
  nand G23 (qb, s_clear_ab, clr_n);

  // Notes on the sheet:
  //   jk_ff | Gate-level only | Same-name tunnels are connected
endmodule

module d_ff_async (
  input  d,
  input  clk,
  input  set,
  input  clr,
  output q,
  output qb
);

  wire clkn, clrn, idle, idle_n, m_dn, m_qrab, m_qrn, m_qsab, m_qsn, m_rb, m_sb, men, men_n, mq, mqb, s_dn,
       s_qrab, s_qrn, s_qsab, s_qsn, s_rb, s_sb, sen, sen_n, setn;

  nand G1 (clkn, clk, clk);
  nand G2 (clrn, clr, clr);
  nand G3 (setn, set, clrn);
  nand G4 (idle_n, clrn, setn);
  nand G5 (idle, idle_n, idle_n);
  nand G6 (men_n, clkn, idle);
  nand G7 (men, men_n, men_n);
  nand G8 (sen_n, clk, idle);
  nand G9 (sen, sen_n, sen_n);
  nand G10 (m_dn, d, d);
  nand G11 (m_sb, d, men);
  nand G12 (m_rb, m_dn, men);
  nand G13 (m_qsn, m_sb, mqb);
  nand G14 (m_qsab, m_qsn, m_qsn);
  nand G15 (mq, m_qsab, setn);
  nand G16 (m_qrn, m_rb, mq);
  nand G17 (m_qrab, m_qrn, m_qrn);
  nand G18 (mqb, m_qrab, clrn);
  nand G19 (s_dn, mq, mq);
  nand G20 (s_sb, mq, sen);
  nand G21 (s_rb, s_dn, sen);
  nand G22 (s_qsn, s_sb, qb);
  nand G23 (s_qsab, s_qsn, s_qsn);
  nand G24 (q, s_qsab, setn);
  nand G25 (s_qrn, s_rb, q);
  nand G26 (s_qrab, s_qrn, s_qrn);
  nand G27 (qb, s_qrab, clrn);

  // Notes on the sheet:
  //   d_ff_async | Gate-level only | Same-name tunnels are connected
endmodule
